// Logisim project ALU_ENCODER.circ as structural Verilog: 1 circuit, main circuit ALU_ENCODER
module ALU_ENCODER (
  input  add,
  input  addi,
  input  slt,
  input  slti,
  input  sltu,
  input  sltiu,
  input  sub,
  input  mult,
  input  multu,
  input  div,
  input  divu,
  input  \and ,
  input  andi,
  input  \or ,
  input  ori,
  input  \xor ,
  input  xori,
  input  \nor ,
  output [3:0] ALU_OP
);

  wire ADD_t, AND_t, OR_t, priority_encoder_1_gs, SLT_t, SLTU_t, XOR_t;
  wire [3:0] priority_encoder_1_out;

  or or_1 (ADD_t, add, addi);
  or or_2 (SLT_t, slt, slti);
  or or_3 (SLTU_t, sltu, sltiu);
  or or_4 (AND_t, \and , andi);
  or or_5 (OR_t, \or , ori);
  or or_6 (XOR_t, \xor , xori);
  Priority_Encoder #(.select(4), .disabled(0)) priority_encoder_1 (
    .in0(ADD_t), .in1(sub), .in2(AND_t), .in3(OR_t), .in4(\nor ), .in5(XOR_t), .in6(SLT_t), .in7(SLTU_t),
    .in8(multu), .in9(mult), .in10(divu), .in11(div), .out(priority_encoder_1_out),
    .gs(priority_encoder_1_gs), .en_in(1'b1));  // open: in12, in13, in14, in15, en_out
  Multiplexer #(.width(4), .disabled(0), .enable("false")) multiplexer_1 (
    .in0(4'b0000), .in1(priority_encoder_1_out), .out(ALU_OP), .sel(priority_encoder_1_gs));
endmodule
