// Logisim project HI-LO Registers.circ as structural Verilog: 1 circuit, main circuit HI/LO Registers
module HI_LO_Registers (
  input  [31:0] Low_in,
  input  [31:0] High_in,
  input  Hi_Lo_enable,
  input  Clock,
  output [31:0] Low_out,
  output [31:0] High_out
);

  Register #(.width(32)) High (.D(High_in), .en(Hi_Lo_enable), .Q(High_out), .clk(Clock));  // open: clr
  Register #(.width(32)) Low (.D(Low_in), .en(Hi_Lo_enable), .Q(Low_out), .clk(Clock));  // open: clr

  // Other names for the same wires on the sheet: CLK = Clock; Hi[31:0] = High_in; HI_LO_EN = Hi_Lo_enable;
  //   Lo[31:0] = Low_in; OutHi[31:0] = High_out; OutLo[31:0] = Low_out

  // Notes on the sheet:
  //   INPUTS
  //   OUTPUTS
endmodule
